// Digital circuit ALU.dig as structural Verilog
module ALU (
  input  [7:0] A,
  input  [7:0] B,
  input  C_i,
  input  [2:0] O_p,
  output [7:0] O,
  output C_o,
  output N,
  output Z
);

  wire add_1_c_o, bitselector_1_out, sub_1_c_o;
  wire [7:0] add_1_s, and_1_out, left_out, not_1_out, or_1_out, right_out, sub_1_s, xor_1_out;

  assign xor_1_out = A ^ B;  // XOr xor_1, 8 bits wide
  assign not_1_out = ~A;  // Not not_1, 8 bits wide
  assign or_1_out = A | B;  // Or or_1, 8 bits wide
  assign and_1_out = A & B;  // And and_1, 8 bits wide
  Add #(.Bits(8)) add_1 (.a(A), .b(B), .c_i(C_i), .s(add_1_s), .c_o(add_1_c_o));
  Sub #(.Bits(8)) sub_1 (.a(A), .b(B), .c_i(C_i), .s(sub_1_s), .c_o(sub_1_c_o));
  BarrelShifter #(.Bits(8), .barrelShifterMode("arithmetic"), .direction("right")) right (
    .in(A), .shift(B[3:0]), .out(right_out));
  BarrelShifter #(.Bits(8), .barrelShifterMode("arithmetic")) left (.in(A), .shift(B[3:0]), .out(left_out));
  Multiplexer multiplexer_1 (.sel(bitselector_1_out), .in_0(add_1_c_o), .in_1(sub_1_c_o), .out(C_o));
  BitSelector #(.Selector_Bits(3)) bitselector_1 (.in(8'h20), .sel(O_p), .out(bitselector_1_out));
  Multiplexer #(.Selector_Bits(3), .Bits(8)) multiplexer_2 (
    .sel(O_p), .in_0(xor_1_out), .in_1(not_1_out), .in_2(or_1_out), .in_3(and_1_out), .in_4(add_1_s),
    .in_5(sub_1_s), .in_6(right_out), .in_7(left_out), .out({N, O[6:0]}));
  nor nor_1 (Z, N, O[6], O[5], O[4], O[3], O[2], O[1], O[0]);

  assign O[7] = N;
endmodule
