// Digital circuit ALUv2.dig as structural Verilog
module ALUv2 (
  input  [7:0] B,
  input  [7:0] A,
  input  [3:0] OP_code,
  output [7:0] Y,
  output [2:0] Flags
);

  wire add_1_c_o, sub_1_c_o;
  wire [7:0] add_1_s, and_1_out, div_1_q, div_1_r, left_out, mul_1_mul, multiplexer_1_out, not_1_out,
       or_1_out, right_out, sub_1_s, xor_1_out;

  Multiplexer #(.Bits(8)) multiplexer_1 (.sel(OP_code[1]), .in_0(B), .in_1(8'h1), .out(multiplexer_1_out));
  Add #(.Bits(8)) add_1 (.a(A), .b(multiplexer_1_out), .c_i(OP_code[0]), .s(add_1_s), .c_o(add_1_c_o));
  Sub #(.Bits(8)) sub_1 (.a(A), .b(multiplexer_1_out), .c_i(OP_code[0]), .s(sub_1_s), .c_o(sub_1_c_o));
  assign and_1_out = A & B;  // And and_1, 8 bits wide
  assign or_1_out = A | B;  // Or or_1, 8 bits wide
  assign not_1_out = ~A;  // Not not_1, 8 bits wide
  assign xor_1_out = A ^ B;  // XOr xor_1, 8 bits wide
  Div #(.Bits(8)) div_1 (.a(A), .b(B), .q(div_1_q), .r(div_1_r));
  BarrelShifter #(.barrelShifterMode("arithmetic"), .Bits(8)) left (.in(A), .shift(B[3:0]), .out(left_out));
  BarrelShifter #(.barrelShifterMode("arithmetic"), .Bits(8), .direction("right")) right (
    .in(A), .shift(B[3:0]), .out(right_out));
  Mul #(.Bits(4)) mul_1 (.a(A[3:0]), .b(B[3:0]), .mul(mul_1_mul));
  Multiplexer #(.Selector_Bits(4), .Bits(8)) multiplexer_2 (
    .sel(OP_code), .in_0(add_1_s), .in_1(add_1_s), .in_2(add_1_s), .in_3(A), .in_4(sub_1_s), .in_5(sub_1_s),
    .in_6(sub_1_s), .in_7(and_1_out), .in_8(or_1_out), .in_9(not_1_out), .in_10(xor_1_out), .in_11(div_1_q),
    .in_12(div_1_r), .in_13(left_out), .in_14(right_out), .in_15(mul_1_mul), .out({Flags[1], Y[6:0]}));
  nor nor_1 (Flags[0], Y[0], Y[1], Y[2], Y[3], Y[5], Y[6], Flags[1], Y[4]);
  Multiplexer multiplexer_3 (.sel(OP_code[2]), .in_0(add_1_c_o), .in_1(sub_1_c_o), .out(Flags[2]));

  assign Y[7] = Flags[1];
endmodule
