// Digital circuit ALUv4.dig as structural Verilog
module ALUv4 (
  input  [15:0] A,
  input  [15:0] B,
  input  C_in,
  input  [3:0] op,
  output C_out,
  output [15:0] Y,
  output Z,
  output S,
  output V
);

  wire add_1_c_o, add_2_c_o, add_3_c_o, and_2_out, and_3_out, comparator_1_gt, comparator_2_gt,
       comparator_2_lt, comparator_3_gt, comparator_3_lt, comparator_4_gt, or_2_out, sub_1_c_o, sub_2_c_o,
       sub_3_c_o;
  wire [15:0] add_1_s, add_2_s, add_3_s, and_1_out, div_1_q, div_1_r, left_out, neg_1_out, or_1_out,
       right_out, sub_1_s, sub_2_s, sub_3_s, xor_1_out;
  wire [31:0] mul_1_mul;

  Add #(.Bits(16)) add_1 (.a(A), .b(B), .c_i(1'b0), .s(add_1_s), .c_o(add_1_c_o));
  Add #(.Bits(16)) add_2 (.a(A), .b(B), .c_i(C_in), .s(add_2_s), .c_o(add_2_c_o));
  Sub #(.Bits(16)) sub_1 (.a(A), .b(B), .c_i(1'b0), .s(sub_1_s), .c_o(sub_1_c_o));
  Sub #(.Bits(16)) sub_2 (.a(A), .b(B), .c_i(C_in), .s(sub_2_s), .c_o(sub_2_c_o));
  Mul #(.Bits(16)) mul_1 (.a(A), .b(B), .mul(mul_1_mul));
  Div #(.Bits(16)) div_1 (.a(A), .b(B), .q(div_1_q), .r(div_1_r));
  assign and_1_out = A & B;  // And and_1, 16 bits wide
  assign or_1_out = A | B;  // Or or_1, 16 bits wide
  assign xor_1_out = A ^ B;  // XOr xor_1, 16 bits wide
  Neg #(.Bits(16)) neg_1 (.in(A), .out(neg_1_out));
  BarrelShifter #(.Bits(16), .barrelShifterMode("arithmetic")) left (.in(A), .shift(B[4:0]), .out(left_out));
  BarrelShifter #(.Bits(16), .barrelShifterMode("arithmetic"), .direction("right")) right (
    .in(A), .shift(B[4:0]), .out(right_out));
  Add #(.Bits(16)) add_3 (.a(A), .b({16{1'b0}}), .c_i(1'b1), .s(add_3_s), .c_o(add_3_c_o));
  Sub #(.Bits(16)) sub_3 (.a(A), .b({16{1'b0}}), .c_i(1'b1), .s(sub_3_s), .c_o(sub_3_c_o));
  Multiplexer #(.Selector_Bits(4)) multiplexer_1 (
    .sel(op), .in_0(1'b0), .in_1(add_1_c_o), .in_2(add_2_c_o), .in_3(sub_1_c_o), .in_4(sub_2_c_o),
    .in_5(1'b0), .in_6(1'b0), .in_7(1'b0), .in_8(1'b0), .in_9(1'b0), .in_10(1'b0), .in_11(1'b0),
    .in_12(1'b0), .in_13(1'b0), .in_14(1'b0), .in_15(1'b0), .out(C_out));
  Multiplexer #(.Selector_Bits(4), .Bits(16)) multiplexer_2 (
    .sel(op), .in_0(B), .in_1(add_1_s), .in_2(add_2_s), .in_3(sub_1_s), .in_4(sub_2_s),
    .in_5(mul_1_mul[15:0]), .in_6(div_1_q), .in_7(div_1_r), .in_8(and_1_out), .in_9(or_1_out),
    .in_10(xor_1_out), .in_11(neg_1_out), .in_12(left_out), .in_13(right_out), .in_14(add_3_s),
    .in_15(sub_3_s), .out(Y));
  Comparator #(.Signed("true"), .Bits(16)) comparator_1 (.a(Y), .b({16{1'b0}}), .gt(comparator_1_gt), .eq(Z), .lt(S));
  Comparator #(.Signed("true"), .Bits(16)) comparator_2 (
    .a(A), .b({16{1'b0}}), .gt(comparator_2_gt), .lt(comparator_2_lt));  // open: eq
  Comparator #(.Signed("true"), .Bits(16)) comparator_3 (
    .a(B), .b({16{1'b0}}), .gt(comparator_3_gt), .lt(comparator_3_lt));  // open: eq
  and and_2 (and_2_out, S, comparator_2_gt, comparator_3_gt);
  and and_3 (and_3_out, comparator_1_gt, comparator_2_lt, comparator_3_lt);
  Comparator #(.Bits(16)) comparator_4 (.a(mul_1_mul[31:16]), .b({16{1'b0}}), .gt(comparator_4_gt));  // open: eq, lt
  or or_2 (or_2_out, and_2_out, and_3_out);
  Multiplexer #(.Selector_Bits(4)) multiplexer_3 (
    .sel(op), .in_0(1'b0), .in_1(or_2_out), .in_2(or_2_out), .in_3(or_2_out), .in_4(or_2_out),
    .in_5(comparator_4_gt), .in_6(1'b0), .in_7(1'b0), .in_8(1'b0), .in_9(1'b0), .in_10(1'b0), .in_11(1'b0),
    .in_12(1'b0), .in_13(1'b0), .in_14(add_3_c_o), .in_15(sub_3_c_o), .out(V));

  // Notes on the sheet:
  //   A: pin 1
  //   B: pin 4
  //   C_in: pin 5
  //   op: pin 2
  //   C_out: pin 6
  //   Y: pin 10
  //   Z: pin 8
  //   S: pin 7
  //   V: pin 9
endmodule
