// Digital circuit CONTROL_UNIT.dig as structural Verilog
module CONTROL_UNIT (
  input  [15:0] in,
  input  C,
  input  in_3,
  input  in_4
);

  wire [1:0] STEP_out;
  wire [4:0] rom_1_d;

  Counter #(.Bits(2)) STEP (.en(in_3), .C(C), .clr(in_4), .out(STEP_out));  // open: ovf
  Counter #(.Bits(3)) STEP_2 (.en(C), .C(C), .clr(C));  // open: out, ovf
  ROM #(.AddrBits(6), .Bits(5)) rom_1 (.A({in[3:0], STEP_out}), .sel(1'b1), .D(rom_1_d));
  Register #(.Bits(3)) reg_a (.D(in[11:9]), .C(C), .en(rom_1_d[0]));  // open: Q
  Register #(.Bits(3)) reg_b (.D(in[15:13]), .C(C), .en(rom_1_d[1]));  // open: Q
  Register #(.Bits(3)) reg_c (.D(in[15:13]), .C(C), .en(rom_1_d[2]));  // open: Q
  Register #(.Bits(16)) const_a (.D(in), .C(C), .en(rom_1_d[3]));  // open: Q
  Register #(.Bits(16)) const_b (.D(in), .C(C), .en(rom_1_d[4]));  // open: Q

  // Notes on the sheet:
  //   contents of rom_1 (hex, n*v repeats v):
  //   3,15*0,3,4,14*0,3
endmodule
