// Digital circuit CPU.dig as structural Verilog
module CPU (
  input  clk
);

  wire button_1_out, INSTR_ovf, not_1_out, PC_ovf;
  wire [2:0] ALU_c_o, FLAG_q;
  wire [3:0] Microcode_d_2;
  wire [7:0] A_q, ALU_o, B_q, INSTR_out, multiplexer_1_out, ROM_d, SP_out;
  wire [15:0] MEM_q, PC_in_q, PC_out;
  wire [15:8] multiplexer_1_out_2;
  wire [23:0] Microcode_d;

  Button button_1 (.out(button_1_out));
  CounterPreset #(.Bits(8)) SP (
    .en(Microcode_d[17]), .C(clk), .dir(not_1_out), .in(multiplexer_1_out), .ld(Microcode_d[16]),
    .clr(button_1_out), .out(SP_out));  // open: ovf
  not not_1 (not_1_out, Microcode_d[0]);
  ROM #(.AddrBits(8), .Bits(24)) Microcode (
    .A(INSTR_out), .sel(1'b1), .D({Microcode_d[23:9], Microcode_d_2, Microcode_d[4:0]}));
  CounterPreset #(.Bits(16), .isProgramCounter("true")) PC (
    .en(Microcode_d[15]), .C(clk), .dir(1'b0), .in(PC_in_q), .ld(Microcode_d[14]), .clr(button_1_out),
    .out(PC_out), .ovf(PC_ovf));
  LED led_1 (.in(PC_ovf));
  // Probe on {multiplexer_1_out_2, multiplexer_1_out}
  LED led_2 (.in(INSTR_ovf));
  SHIFT_REG PC_in (.D(ROM_d), .en(Microcode_d[13]), .C(clk), .Q(PC_in_q));
  ROM #(.AddrBits(16), .isProgramMemory("true"), .Bits(8)) ROM (.A(PC_out), .sel(Microcode_d[18]), .D(ROM_d));
  Multiplexer #(.Bits(16)) multiplexer_1 (
    .sel(Microcode_d[17]), .in_0(MEM_q), .in_1({{8{1'b0}}, SP_out}),
    .out({multiplexer_1_out_2, multiplexer_1_out}));
  CounterPreset #(.Bits(8)) INSTR (
    .en(1'b1), .C(clk), .dir(1'b0), .in(ROM_d), .ld(Microcode_d[2]), .clr(button_1_out), .out(INSTR_out),
    .ovf(INSTR_ovf));
  assign ROM_d = Microcode_d[22] ? PC_out[7:0] : 8'bz;  // Driver driver_1
  SHIFT_REG MEM (.D(ROM_d), .en(Microcode_d[19]), .C(clk), .Q(MEM_q));
  assign ROM_d = Microcode_d[20] ? MEM_q[15:8] : 8'bz;  // Driver driver_2
  RAMDualPort #(.AddrBits(16), .Bits(8)) RAM (
    .A({multiplexer_1_out_2, multiplexer_1_out}), .Din(ROM_d), .str(Microcode_d[0]), .C(clk),
    .ld(Microcode_d[1]), .D(ROM_d));
  assign ROM_d = Microcode_d[21] ? PC_out[15:8] : 8'bz;  // Driver driver_3
  // Probe BUS on ROM_d
  assign ROM_d = Microcode_d[11] ? B_q : 8'bz;  // Driver driver_4
  Register #(.Bits(8)) B (.D(ROM_d), .C(clk), .en(Microcode_d[12]), .Q(B_q));
  ROM #(.AddrBits(6), .Bits(8)) Decoder (.A({INSTR_out[2:0], FLAG_q}), .sel(Microcode_d[10]), .D(ROM_d));
  assign ROM_d = Microcode_d[9] ? ALU_o : 8'bz;  // Driver driver_5
  Register #(.Bits(8)) A (.D(ROM_d), .C(clk), .en(Microcode_d[3]), .Q(A_q));
  assign ROM_d = Microcode_d[4] ? A_q : 8'bz;  // Driver driver_6
  Terminal terminal_1 (.D(ROM_d), .C(clk), .en(Microcode_d[23]));
  Register #(.Bits(3)) FLAG (.D(ALU_c_o), .C(clk), .en(Microcode_d[9]), .Q(FLAG_q));
  ALU ALU (
    .A(A_q), .B(B_q), .C_i(Microcode_d_2[0]), .O_p(Microcode_d_2[3:1]), .O(ALU_o), .C_o(ALU_c_o[2]),
    .N(ALU_c_o[1]), .Z(ALU_c_o[0]));

  // Notes on the sheet:
  //   clk: Hz: 5
  //   contents of Microcode (hex, n*v repeats v):
  //   0,48004,48008,48004,49000,48004,c8000,c8000,a,48004,c8000,c8000
  //   ,1002,48004,c8000,c8000,11,48004,c8000,c8000,801,48004,308,48004
  //   ,328,48004,348,48004,368,48004,2c8,48004,288,48004,208,48004,248
  //   ,48004,3c8,48004,388,48004,340,48004,20011,48004,20000,2000a,68005
  //   ,4a000,4a000,420001,224001,48004,20000,22002,22002,4000,48004
  //   ,6*404,8000,8000,48004,80000,c8000,58004,800010,48004
  //   contents of ROM (hex, n*v repeats v):
  //   2,1,4,1,e,ff,ff,16,a,ff,ff,2c,2,29,2a,2e,3d,0,4,47,12,ff,ff,6
  //   ,ff,ff,47
  //   contents of Decoder (hex, n*v repeats v):
  //   4*41,4*31,16*0,31,41,31,41,31,41,31,41,41,31,41,31,41,31,41,31,31,31
  //   ,41,41,31,31,4*41,31,31,41,41,6*31,4*41
endmodule
