// Digital circuit CPUv2.dig as structural Verilog
module CPUv2 (
  input  Ck,
  input  [7:0] in_4,
  output [7:0] out_2,
  output [3:0] out_3
);

  wire add_1_c_o, add_2_c_o, add_3_c_o, and_1_out, INT_q, IR_ovf, IRQ_out, NMI_out, not_1_out, not_2_out,
       or_1_out, or_2_out, PC_ovf, SP_ovf, t_ff_1_nq, X_ovf;
  wire [2:0] FLAG_q, IR_out, undriven;
  wire [7:0] A_q, B_q, driver_5_out, EXT_AR_q, multiplexer_1_out, Program_d, TMP_q, undriven_2, X_out;
  wire [7:3] IR_out_2;
  wire [7:4] add_2_s;
  wire [15:0] add_1_s, add_3_s, driver_1_out, MEM_AR_q, multiplexer_2_out, multiplexer_3_out, PC_out, SP_out;
  wire [31:0] Microcode_d;

  T_FF t_ff_1 (.T(Microcode_d[12]), .C(Ck), .nQ(t_ff_1_nq));  // open: Q
  and and_1 (and_1_out, t_ff_1_nq, IRQ_out);
  Button IRQ (.out(IRQ_out));
  ALUv2 ALU ();
  Button NMI (.out(NMI_out));
  Register #(.Bits(8)) B (.D(driver_1_out[7:0]), .C(Ck), .en(Microcode_d[11]), .Q(B_q));
  LED led_1 (.in(IR_ovf));
  ROM #(.AddrBits(8), .Bits(32)) Microcode (.A({IR_out_2, IR_out}), .sel(1'b1), .D(Microcode_d));
  or or_1 (or_1_out, and_1_out, NMI_out);
  CounterPreset #(.Bits(8)) IR (
    .en(1'b1), .C(Ck), .dir(1'b0), .in(multiplexer_1_out), .ld(Microcode_d[0]), .clr(1'b0),
    .out({IR_out_2, IR_out}), .ovf(IR_ovf));
  RS_FF INT (.S(or_1_out), .C(Ck), .R(Microcode_d[0]), .Q(INT_q));  // open: nQ
  assign driver_1_out[7:0] = Microcode_d[31] ? undriven_2 : 8'bz;  // Driver driver_1
  Register #(.Bits(3)) FLAG (.D(undriven), .C(Ck), .en(Microcode_d[31]), .Q(FLAG_q));
  ROM #(.AddrBits(6), .Bits(8)) FLAG_2 (.A({IR_out, FLAG_q}), .sel(Microcode_d[22]), .D(driver_1_out[15:8]));
  assign driver_1_out[7:0] = Microcode_d[20] ? B_q : 8'bz;  // Driver driver_2
  assign driver_1_out[7:0] = Microcode_d[15] ? A_q : 8'bz;  // Driver driver_3
  Register #(.Bits(8)) A (.D(driver_1_out[7:0]), .C(Ck), .en(Microcode_d[14]), .Q(A_q));
  not not_1 (not_1_out, INT_q);
  // Probe BUS_bot on driver_1_out[7:0]
  Multiplexer #(.Bits(8)) multiplexer_1 (
    .sel(not_1_out), .in_0({8{1'b0}}), .in_1(driver_1_out[15:8]), .out(multiplexer_1_out));
  assign driver_1_out[7:0] = Microcode_d[7] ? Program_d : 8'bz;  // Driver driver_4
  // Probe BUS_top on driver_1_out[15:8]
  LED led_2 (.in(INT_q));
  assign driver_5_out = Microcode_d[29] ? driver_1_out[7:0] : 8'bz;  // Driver driver_5
  or or_2 (or_2_out, Microcode_d[29], Microcode_d[30]);
  assign driver_5_out = Microcode_d[30] ? driver_1_out[15:8] : 8'bz;  // Driver driver_6
  assign driver_1_out[7:0] = Microcode_d[27] ? TMP_q : 8'bz;  // Driver driver_7
  assign driver_1_out[15:8] = Microcode_d[28] ? TMP_q : 8'bz;  // Driver driver_8
  RAMSinglePort #(.AddrBits(16), .Bits(8)) RAM (
    .A(multiplexer_2_out), .str(Microcode_d[2]), .C(Ck), .ld(Microcode_d[1]), .D(driver_1_out[7:0]));
  Register #(.Bits(16)) MEM_AR (.D(driver_1_out), .C(Ck), .en(Microcode_d[3]), .Q(MEM_AR_q));
  assign driver_1_out[15:8] = Microcode_d[6] ? Program_d : 8'bz;  // Driver driver_9
  assign driver_1_out = Microcode_d[8] ? PC_out : 16'bz;  // Driver driver_10
  Register #(.Bits(8)) TMP (.D(driver_5_out), .C(Ck), .en(or_2_out), .Q(TMP_q));
  LED led_3 (.in(SP_ovf));
  Multiplexer #(.Bits(16)) multiplexer_2 (
    .sel(Microcode_d[23]), .in_0(add_1_s), .in_1(SP_out), .out(multiplexer_2_out));
  CounterPreset #(.Bits(8)) X (
    .en(Microcode_d[4]), .C(Ck), .dir(1'b0), .in(driver_1_out[7:0]), .ld(Microcode_d[5]),
    .clr(Microcode_d[25]), .out(X_out), .ovf(X_ovf));
  Register #(.Bits(8)) EXT_AR (.D(driver_1_out[7:0]), .C(Ck), .en(Microcode_d[26]), .Q(EXT_AR_q));
  EEPROM #(.AddrBits(16), .isProgramMemory("true"), .Bits(8)) Program (
    .A(add_3_s), .CS(1'b1), .WE(1'b0), .OE(1'b1), .D(Program_d));
  not not_2 (not_2_out, Microcode_d[2]);
  CounterPreset #(.maxValue(128), .Bits(16)) SP (
    .en(Microcode_d[23]), .C(Ck), .dir(not_2_out), .in({{8{1'b0}}, driver_1_out[7:0]}), .ld(Microcode_d[24]),
    .clr(1'b0), .out(SP_out), .ovf(SP_ovf));
  LED led_4 (.in(add_1_c_o));
  Add #(.Bits(16)) add_1 (.a(MEM_AR_q), .b({{8{1'b0}}, X_out}), .c_i(1'b0), .s(add_1_s), .c_o(add_1_c_o));
  LED led_5 (.in(X_ovf));
  Add #(.Bits(8)) add_2 (.a(X_out), .b(EXT_AR_q), .c_i(1'b0), .s({add_2_s, out_3}), .c_o(add_2_c_o));
  LED led_6 (.in(add_3_c_o));
  LED led_7 (.in(add_2_c_o));
  Add #(.Bits(16)) add_3 (.a(PC_out), .b({{8{1'b0}}, X_out}), .c_i(1'b0), .s(add_3_s), .c_o(add_3_c_o));
  CounterPreset #(.Bits(16), .isProgramCounter("true")) PC (
    .en(Microcode_d[9]), .C(Ck), .dir(1'b0), .in(multiplexer_3_out), .ld(Microcode_d[10]), .clr(1'b0),
    .out(PC_out), .ovf(PC_ovf));
  assign driver_1_out[7:0] = Microcode_d[21] ? in_4 : 8'bz;  // Driver driver_11
  assign out_2 = Microcode_d[13] ? driver_1_out[7:0] : 8'bz;  // Driver driver_12
  LED led_8 (.in(PC_ovf));
  Multiplexer #(.Bits(16)) multiplexer_3 (.sel(INT_q), .in_0(driver_1_out), .in_1({16{1'b0}}), .out(multiplexer_3_out));

  // Notes on the sheet:
  //   Ck: Hz: 2147483647
  //   contents of Microcode (hex, n*v repeats v):
  //   0,241,4280,241,a80,241,2a0,241,251,40000240,10000288,8245,40000240
  //   ,10000288,100245,20008000,104000,8000a41,40000240,10000288,4243
  //   ,40000240,10000288,a43
  //   contents of Program (hex, n*v repeats v):
  //   2,29,4,37,f,f
endmodule
