// Digital circuit CPUv3.dig as structural Verilog
module CPUv3 (
  input  clk,
  input  [7:0] in_4,
  output [7:0] out_2,
  output out_3
);

  wire and_1_out, button_1_out, button_2_out, decoder_1_out_14, decoder_1_out_15, demultiplexer_2_out_0,
       demultiplexer_2_out_1, demultiplexer_3_out_0, demultiplexer_3_out_1, demultiplexer_4_out_0,
       demultiplexer_4_out_1, int_handler_1_int, int_handler_1_s, IR_ovf, keyboard_1_av, monoflop_1_q,
       not_1_out, or_1_out, or_2_out, pulse_extend_1_out, rs_ff_1_nq, rs_ff_1_q;
  wire [1:0] undriven;
  wire [3:0] driver_1_out, EXT_AR_q, FLAG_q, Microcode_d_2, multiplexer_4_out;
  wire [7:0] A_q, B_q, demultiplexer_1_out_15, driver_4_out, keyboard_1_d, multiplexer_1_out,
       multiplexer_2_out, multiplexer_3_out, multiplexer_5_out, multiplexer_6_out, notconnected_1_out,
       Program_d, ramdualport_1_d, SP_out, TMP_q, undriven_2, X_out;
  wire [7:2] IR_out;
  wire [15:0] add_1_s, MEM_AR_q, multiplexer_7_out, multiplexer_8_out, multiplexer_9_out, PC_out;
  wire [15:4] driver_1_out_2;
  wire [15:8] keyboard_1_d_2;
  wire [30:0] Microcode_d;

  Button button_1 (.out(button_1_out));
  Monoflop monoflop_1 (.C(button_1_out), .R(int_handler_1_int), .Q(monoflop_1_q));  // open: nQ
  or or_1 (or_1_out, keyboard_1_av, monoflop_1_q);
  and and_1 (and_1_out, int_handler_1_int, ~Microcode_d[30]);  // And
  assign {driver_1_out_2[7:4], driver_1_out} = Microcode_d[15] ? multiplexer_3_out : 8'bz;  // Driver driver_1
  INT_HANDLER int_handler_1 (
    .INT_en(Microcode_d[23]), .IRQ(or_1_out), .C(clk), .INT(int_handler_1_int), .S(int_handler_1_s));
  Multiplexer #(.Bits(8)) multiplexer_1 (
    .sel(rs_ff_1_q), .in_0(multiplexer_2_out), .in_1(8'h99), .out(multiplexer_1_out));
  LED led_1 (.in(int_handler_1_s));
  LED led_2 (.in(int_handler_1_int));
  Multiplexer #(.Bits(8)) multiplexer_2 (
    .sel(and_1_out), .in_0(driver_1_out_2[15:8]), .in_1(8'h88), .out(multiplexer_2_out));
  or or_2 (or_2_out, int_handler_1_int, button_2_out);
  RS_FF rs_ff_1 (.S(IR_ovf), .C(~clk), .R(or_2_out), .Q(rs_ff_1_q), .nQ(rs_ff_1_nq));
  LED led_3 (.in(rs_ff_1_q));
  ALUv2 aluv2_1 ();
  Keyboard keyboard_1 (.C(clk), .en(decoder_1_out_14), .D({keyboard_1_d_2, keyboard_1_d}), .av(keyboard_1_av));
  // NotConnected on notconnected_1_out
  Multiplexer #(.Selector_Bits(4), .Bits(8)) multiplexer_3 (
    .sel(EXT_AR_q), .in_0(in_4), .in_1(notconnected_1_out), .in_2(notconnected_1_out),
    .in_3(notconnected_1_out), .in_4(notconnected_1_out), .in_5(notconnected_1_out),
    .in_6(notconnected_1_out), .in_7(notconnected_1_out), .in_8(notconnected_1_out),
    .in_9(notconnected_1_out), .in_10(notconnected_1_out), .in_11(notconnected_1_out),
    .in_12(notconnected_1_out), .in_13(notconnected_1_out), .in_14(keyboard_1_d), .in_15(notconnected_1_out),
    .out(multiplexer_3_out));
  Demultiplexer #(.Selector_Bits(4), .Bits(8)) demultiplexer_1 (
    .sel(EXT_AR_q), .in(driver_4_out), .out_0(out_2), .out_15(demultiplexer_1_out_15));  // open: out_1, out_2, out_3, out_4, out_5, out_6, out_7, out_8, out_9, out_10, out_11, out_12, out_13, out_14
  ROM #(.AddrBits(4), .Bits(8)) FLAG_Decoder (.A(FLAG_q), .sel(Microcode_d[30]), .D(driver_1_out_2[15:8]));
  Register #(.Bits(4)) EXT_AR (.D(multiplexer_4_out), .C(clk), .en(1'b1), .Q(EXT_AR_q));
  CounterPreset #(.Bits(8)) X (
    .en(Microcode_d[27]), .C(clk), .dir(1'b0), .in({driver_1_out_2[7:4], driver_1_out}),
    .ld(Microcode_d[28]), .clr(1'b0), .out(X_out));  // open: ovf
  Register #(.Bits(2)) FLAG (.D(undriven), .C(clk), .en(Microcode_d[26]), .Q(FLAG_q[1:0]));
  assign {driver_1_out_2[7:4], driver_1_out} = Microcode_d[25] ? A_q : 8'bz;  // Driver driver_2
  assign {driver_1_out_2[7:4], driver_1_out} = Microcode_d[24] ? B_q : 8'bz;  // Driver driver_3
  Register #(.Bits(8)) B (.D({driver_1_out_2[7:4], driver_1_out}), .C(clk), .en(Microcode_d[17]), .Q(B_q));
  Register #(.Bits(8)) A (.D({driver_1_out_2[7:4], driver_1_out}), .C(clk), .en(Microcode_d[16]), .Q(A_q));
  assign driver_4_out = Microcode_d[18] ? {driver_1_out_2[7:4], driver_1_out} : 8'bz;  // Driver driver_4
  Multiplexer #(.Bits(4)) multiplexer_4 (
    .sel(Microcode_d[22]), .in_0(4'b0000), .in_1(driver_1_out), .out(multiplexer_4_out));
  assign {driver_1_out_2[7:4], driver_1_out} = Microcode_d[29] ? X_out : 8'bz;  // Driver driver_5
  assign {driver_1_out_2[7:4], driver_1_out} = Microcode_d[26] ? undriven_2 : 8'bz;  // Driver driver_6
  Multiplexer #(.Bits(8)) multiplexer_5 (
    .sel(Microcode_d[8]), .in_0(driver_1_out_2[15:8]), .in_1({driver_1_out_2[7:4], driver_1_out}),
    .out(multiplexer_5_out));
  assign {driver_1_out_2[7:4], driver_1_out} = demultiplexer_2_out_1 ? ramdualport_1_d : 8'bz;  // Driver driver_7
  assign driver_1_out_2[15:8] = demultiplexer_2_out_0 ? ramdualport_1_d : 8'bz;  // Driver driver_8
  assign {driver_1_out_2, driver_1_out} = Microcode_d[13] ? 16'h2 : 16'bz;  // Driver driver_9
  Register #(.Bits(16)) MEM_AR (.D({driver_1_out_2, driver_1_out}), .C(clk), .en(Microcode_d[6]), .Q(MEM_AR_q));
  assign {driver_1_out_2[7:4], driver_1_out} = demultiplexer_3_out_1 ? Program_d : 8'bz;  // Driver driver_10
  assign driver_1_out_2[15:8] = demultiplexer_3_out_0 ? Program_d : 8'bz;  // Driver driver_11
  assign {driver_1_out_2, driver_1_out} = Microcode_d[2] ? PC_out : 16'bz;  // Driver driver_12
  CounterPreset #(.maxValue(153), .Bits(8)) IR (
    .en(rs_ff_1_nq), .C(clk), .dir(1'b0), .in(multiplexer_1_out), .ld(Microcode_d[10]), .clr(button_2_out),
    .out({IR_out, FLAG_q[3:2]}), .ovf(IR_ovf));
  Decoder #(.Selector_Bits(4)) decoder_1 (
    .sel(EXT_AR_q), .out_0(out_3), .out_14(decoder_1_out_14), .out_15(decoder_1_out_15));  // open: out_1, out_2, out_3, out_4, out_5, out_6, out_7, out_8, out_9, out_10, out_11, out_12, out_13
  RAMDualPort #(.AddrBits(16), .Bits(8)) ramdualport_1 (
    .A(multiplexer_7_out), .Din(multiplexer_5_out), .str(Microcode_d[9]), .C(clk), .ld(1'b1),
    .D(ramdualport_1_d));
  Add #(.Bits(16)) add_1 (.a(MEM_AR_q), .b({{8{1'b0}}, X_out}), .c_i(1'b0), .s(add_1_s));  // open: c_o
  CounterPreset #(.Bits(16), .isProgramCounter("true")) PC (
    .en(Microcode_d[0]), .C(clk), .dir(Microcode_d[23]), .in({driver_1_out_2, driver_1_out}),
    .ld(Microcode_d[1]), .clr(button_2_out), .out(PC_out));  // open: ovf
  Multiplexer #(.Bits(8)) multiplexer_6 (
    .sel(Microcode_d[11]), .in_0(driver_1_out_2[15:8]), .in_1({driver_1_out_2[7:4], driver_1_out}),
    .out(multiplexer_6_out));
  Multiplexer #(.Bits(16)) multiplexer_7 (
    .sel(pulse_extend_1_out), .in_0(multiplexer_8_out), .in_1({{8{1'b0}}, SP_out}), .out(multiplexer_7_out));
  Multiplexer #(.Bits(16)) multiplexer_8 (
    .sel(Microcode_d[7]), .in_0(MEM_AR_q), .in_1(add_1_s), .out(multiplexer_8_out));
  EEPROM #(.AddrBits(16), .isProgramMemory("true"), .Bits(8)) Program (
    .A(multiplexer_9_out), .CS(1'b1), .WE(1'b0), .OE(1'b1), .D(Program_d));
  Multiplexer #(.Bits(16)) multiplexer_9 (
    .sel(Microcode_d[3]), .in_0(PC_out), .in_1(multiplexer_8_out), .out(multiplexer_9_out));
  ROM #(.AddrBits(8), .Bits(35)) Microcode (.A({IR_out, FLAG_q[3:2]}), .sel(1'b1), .D({Microcode_d_2, Microcode_d}));
  Register #(.Bits(8)) TMP (.D(multiplexer_6_out), .C(clk), .en(Microcode_d[14]), .Q(TMP_q));
  CounterPreset #(.Bits(8)) SP (
    .en(Microcode_d[20]), .C(clk), .dir(not_1_out), .in({driver_1_out_2[7:4], driver_1_out}),
    .ld(Microcode_d[21]), .clr(1'b0), .out(SP_out));  // open: ovf
  Demultiplexer demultiplexer_2 (
    .sel(Microcode_d[8]), .in(Microcode_d[19]), .out_0(demultiplexer_2_out_0), .out_1(demultiplexer_2_out_1));
  PULSE_EXTEND pulse_extend_1 (.C(clk), .in(Microcode_d[20]), .out(pulse_extend_1_out));
  Demultiplexer demultiplexer_3 (
    .sel(Microcode_d[4]), .in(Microcode_d[5]), .out_0(demultiplexer_3_out_0), .out_1(demultiplexer_3_out_1));
  Terminal #(.termHeight(10)) terminal_1 (.D(demultiplexer_1_out_15), .C(clk), .en(decoder_1_out_15));
  assign {driver_1_out_2[7:4], driver_1_out} = demultiplexer_4_out_1 ? TMP_q : 8'bz;  // Driver driver_13
  assign driver_1_out_2[15:8] = demultiplexer_4_out_0 ? TMP_q : 8'bz;  // Driver driver_14
  Demultiplexer demultiplexer_4 (
    .sel(Microcode_d[11]), .in(Microcode_d[12]), .out_0(demultiplexer_4_out_0), .out_1(demultiplexer_4_out_1));
  not not_1 (not_1_out, Microcode_d[9]);
  Button button_2 (.out(button_2_out));

  // Notes on the sheet:
  //   clk: Hz: 50
  //   contents of FLAG_Decoder (hex, n*v repeats v):
  //   7c,76,7c,76,76,7c,76,7c,7c,7c,4*76,7c,7c
  //   contents of Program (hex, n*v repeats v):
  //   0,17,5c,5a,8,0,10,0,2b,73,78,0,13,3c,f,63,75,0,6,5d,71,61,8c,8
  //   ,1,58,6,2a,3e,f,72,73,79,0,1c,6,a,3e,f,63,75,0,19,43,6c,61,79
  //   ,20,69,73,20,61,20,62,69,74,63,68
  //   contents of Microcode (hex, n*v repeats v):
  //   4021,1032,0,421,10031,421,20031,421,10000031,421,200031,421,4021
  //   ,1071,10038,421,4021,1071,100b8,421,4021,1071,20038,421,4021,1071
  //   ,200b8,421,4021,1071,10000038,421,4021,1071,100000b8,421,4021
  //   ,1071,90521,4021,1071,905a1,4021,1071,a0521,4021,1071,a05a1,4021
  //   ,1071,10080521,4021,1071,100805a1,400031,18421,400031,28421,400031
  //   ,10008421,400031,2040421,400031,1040421,400031,20040421,4021,1071
  //   ,2000721,4021,1071,20007a1,4021,1071,1000721,4021,1071,10007a1
  //   ,4021,1071,20000721,4021,1071,200007a1,2020421,12000421,1010421
  //   ,11000421,20010421,20020421,2100721,1100721,20100721,100000,90521
  //   ,100000,a0521,100000,10080521,8000421,4010421,84010421,204010421
  //   ,284010421,784010421,584010421,604010421,384010421,404010421,484010421
  //   ,504010421,704010421,684010421,104010421,304010421,184010421,204000421
  //   ,4021,1032,421,4*40004c31,1,421,4021,100244,100304,103a,421,100000
  //   ,184000,81802,1,421,900204,100304,2002,421,100000,184000,881802
  //   ,800001,421,800000,0,421,800000,800000,0,421,1,400
endmodule
