// Digital circuit CPUv4.dig as structural Verilog
module CPUv4 (
  input  c,
  input  rd,
  output [15:0] bus_out,
  output [15:0] addr_out,
  output [7:0] instr_out
);

  wire and_1_out, and_2_out, and_3_out, and_4_out, button_1_out, clock, d_ff_as_1_q, demultiplexer_1_out_0,
       demultiplexer_1_out_1, flag_en, flag_out, flag_str, hlt, i_o_in, i_o_out, instr_str, \int , int_en,
       irq, jmp_en, mem_out, mem_str, multiplexer_5_out, not_1_out, not_2_out, not_3_out, not_4_out,
       not_5_out, not_6_out, not_7_out, not_9_out, or_2_out, or_3_out, pc_en, pc_out, pc_str, reg_out,
       reg_str, sp_da, tx_da;
  wire [1:0] step_out;
  wire [3:0] alu_op, jmp_ctrl, multiplexer_4_out, reg_des, reg_src;
  wire [7:0] telnet_1_out;
  wire [7:4] instr_q;
  wire [14:0] multiplexer_11_out;
  wire [14:4] flag_q;
  wire [15:0] aluv4_1_v, driver_5_out, multiplexer_1_out, multiplexer_2_out, multiplexer_3_out,
       multiplexer_7_out, multiplexer_8_out, multiplexer_9_out, multiplexer_10_out, pc_out_2,
       registerfile_1_da, registerfile_1_db, sub_1_s;

  assign bus_out = jmp_en ? multiplexer_1_out : 16'bz;  // Driver driver_1
  D_FF_AS d_ff_as_1 (.Set(rd), .D(rd), .C(and_3_out), .Clr(1'b0), .Q(d_ff_as_1_q));  // open: nQ
  and and_1 (and_1_out, d_ff_as_1_q, c);
  or or_1 (clock, and_1_out, button_1_out);
  Button button_1 (.out(button_1_out));
  and and_2 (and_2_out, irq, \int );
  and and_3 (and_3_out, ~jmp_en, instr_str);  // And
  Multiplexer #(.Bits(16)) multiplexer_1 (
    .sel(multiplexer_5_out), .in_0(16'h1d00), .in_1(16'h1b00), .out(multiplexer_1_out));
  Multiplexer #(.Bits(16)) multiplexer_2 (
    .sel(and_2_out), .in_0(multiplexer_3_out), .in_1(16'h2100), .out(multiplexer_2_out));
  Register #(.Bits(16)) instr (.D(multiplexer_2_out), .C(clock), .en(instr_str), .Q({instr_out, instr_q, reg_src}));
  Multiplexer #(.Bits(16)) multiplexer_3 (.sel(hlt), .in_0(bus_out), .in_1(16'h2600), .out(multiplexer_3_out));
  not not_1 (not_1_out, hlt);
  not not_2 (not_2_out, tx_da);
  Multiplexer #(.Bits(4)) multiplexer_4 (.sel(not_2_out), .in_0(4'b1111), .in_1(reg_des), .out(multiplexer_4_out));
  Multiplexer #(.Selector_Bits(3)) multiplexer_5 (
    .sel(reg_src[2:0]), .in_0(jmp_ctrl[0]), .in_1(not_6_out), .in_2(jmp_ctrl[1]), .in_3(not_5_out),
    .in_4(jmp_ctrl[2]), .in_5(not_4_out), .in_6(jmp_ctrl[3]), .in_7(not_3_out), .out(multiplexer_5_out));
  Counter #(.Bits(2)) step (.en(not_1_out), .C(clock), .clr(instr_str), .out(step_out));  // open: ovf
  or or_2 (or_2_out, i_o_in, mem_out);
  not not_3 (not_3_out, jmp_ctrl[3]);
  not not_4 (not_4_out, jmp_ctrl[2]);
  not not_5 (not_5_out, jmp_ctrl[1]);
  not not_6 (not_6_out, jmp_ctrl[0]);
  not not_7 (not_7_out, sp_da);
  Multiplexer #(.Bits(4)) multiplexer_6 (.sel(not_7_out), .in_0(4'b0000), .in_1(instr_q), .out(reg_des));
  Multiplexer #(.Bits(16)) multiplexer_7 (.sel(or_2_out), .in_0(addr_out), .in_1(bus_out), .out(multiplexer_7_out));
  RegisterFile #(.AddrBits(4), .Bits(16)) registerfile_1 (
    .Din(multiplexer_7_out), .we(reg_str), .Rw(multiplexer_4_out), .C(clock), .Ra(reg_des), .Rb(reg_src),
    .Da(registerfile_1_da), .Db(registerfile_1_db));
  ROM #(.AddrBits(10), .Bits(22)) rom_1 (
    .A({instr_out, step_out}), .sel(1'b1),
    .D({hlt, int_en, jmp_en, tx_da, sp_da, i_o_in, i_o_out, flag_out, flag_str, flag_en, alu_op, reg_str, reg_out, mem_str, mem_out, instr_str, pc_str, pc_out, pc_en}));
  assign bus_out = reg_out ? registerfile_1_db : 16'bz;  // Driver driver_2
  Multiplexer #(.Bits(16)) multiplexer_8 (
    .sel(reg_out), .in_0(registerfile_1_db), .in_1(registerfile_1_da), .out(multiplexer_8_out));
  ALUv4 aluv4_1 (
    .A(registerfile_1_da), .B(multiplexer_8_out), .C_in(jmp_ctrl[0]), .op(alu_op), .C_out(aluv4_1_v[0]),
    .Y(addr_out), .Z(aluv4_1_v[2]), .S(aluv4_1_v[1]), .V(aluv4_1_v[3]));
  Multiplexer #(.Bits(16)) multiplexer_9 (
    .sel(flag_str), .in_0({aluv4_1_v[15], {11{1'b0}}, aluv4_1_v[3:0]}), .in_1(bus_out),
    .out(multiplexer_9_out));
  Multiplexer #(.Bits(16)) multiplexer_10 (.sel(int_en), .in_0(bus_out), .in_1(16'h2), .out(multiplexer_10_out));
  and and_4 (and_4_out, mem_out, ~pc_en);  // And
  not not_8 (aluv4_1_v[15], \int );
  Register u_int (.D(multiplexer_9_out[15]), .C(clock), .en(int_en), .Q(\int ));
  not not_9 (not_9_out, addr_out[15]);
  Demultiplexer demultiplexer_1 (
    .sel(not_9_out), .in(and_4_out), .out_0(demultiplexer_1_out_0), .out_1(demultiplexer_1_out_1));
  CounterPreset #(.Bits(16), .isProgramCounter("true")) pc (
    .en(pc_en), .C(clock), .dir(1'b0), .in(multiplexer_10_out), .ld(pc_str), .clr(1'b0), .out(pc_out_2));  // open: ovf
  Register #(.Bits(15)) flag (.D(multiplexer_9_out[14:0]), .C(clock), .en(flag_en), .Q({flag_q, jmp_ctrl}));
  or or_3 (or_3_out, demultiplexer_1_out_1, pc_en);
  RAMSinglePort #(.AddrBits(15), .Bits(16)) ramsingleport_1 (
    .A(addr_out[14:0]), .str(mem_str), .C(clock), .ld(demultiplexer_1_out_0), .D(bus_out));
  Multiplexer #(.Bits(15)) multiplexer_11 (
    .sel(demultiplexer_1_out_1), .in_0(pc_out_2[14:0]), .in_1(addr_out[14:0]), .out(multiplexer_11_out));
  assign bus_out = flag_out ? {\int , flag_q, jmp_ctrl} : 16'bz;  // Driver driver_3
  Sub #(.Bits(16)) sub_1 (.a(pc_out_2), .b({16{1'b0}}), .c_i(1'b1), .s(sub_1_s));  // open: c_o
  ROM #(.AddrBits(15), .Bits(16)) rom_2 (.A(multiplexer_11_out), .sel(or_3_out), .D(bus_out));
  assign bus_out = pc_out ? sub_1_s : 16'bz;  // Driver driver_4
  assign driver_5_out = i_o_out ? bus_out : 16'bz;  // Driver driver_5
  Telnet telnet_1 (.in(driver_5_out[7:0]), .C(clock), .wr(i_o_out), .rd(i_o_in), .out(telnet_1_out), .av(irq));
  assign bus_out = i_o_in ? {{8{1'b0}}, telnet_1_out} : 16'bz;  // Driver driver_6

  // Other names for the same wires on the sheet: instr[7:0] = instr_out; addr[15:0] = addr_out; bus[15:0] = bus_out

  // Notes on the sheet:
  //   c: Hz: 5000
  //   rd: default 1
  //   contents of rom_1 (hex, n*v repeats v):
  //   9,0,0,0,91,9,0,0,89,0,0,0,60,9,0,0,90,9,0,0,20fe0,9,0,0,24fa0
  //   ,9,0,0,90,20e89,0,0,3010,20e89,0,0,1189,0,0,0,1289,0,0,0,1389
  //   ,0,0,0,1489,0,0,0,1589,0,0,0,1689,0,0,0,1789,0,0,0,41780,1689
  //   ,0,0,1889,0,0,0,1989,0,0,0,1a89,0,0,0,1c89,0,0,0,1d89,0,0,0,1309
  //   ,0,0,0,1009,0,0,0,1e89,0,0,0,1f89,0,0,0,1b89,0,0,0,5,9,0,0,80008
  //   ,0,0,0,1,9,0,0,20fa2,5,9,0,20014,20e81,9,0,100009,0,0,0,20fa2
  //   ,124fa4,9,0,123010,20e80,20014,20e89,8040,9,0,0,10080,9,0,0,200009
  //   ,0,0,0,200008
  //   contents of rom_2 (hex, n*v repeats v):
  //   1b00,fb,511,210,588,5cc,5dd,5ee,2488,1dd,1b,168d,1c05,16,1dd,ff
  //   ,2488,168d,1c05,10,1b00,2d,1788,1c04,2d,1cc,8001,4cc,1dd,8003
  //   ,9dc,18cc,1ee,8023,16de,1c05,29,1dd,8003,1cc,1,3d8,1ee,8001,3ec
  //   ,7e0,7d0,7c0,780,201,710,2200,5b,33,4a,0,5b,32,4a,0,5b,30,3b,30
  //   ,48,0,511,210,544,555,251,144,2,954,455,144,1b,2344,445,2344,1855
  //   ,445,1744,1c05,4f,750,740,201,710,1f00,511,210,544,144,38,544
  //   ,1e00,42,144,34,544,1e00,42,144,3c,544,1e00,42,144,3,904,740,201
  //   ,710,1f00,41,4f,53,7c,3e,20,0,511,210,544,522,122,73,442,1822
  //   ,1744,2344,1c05,80,720,740,201,710,1f00,511,210,544,555,566,577
  //   ,5cc,1cc,8000,4cc,155,8002,455,166,8001,466,1665,1c04,e2,144,8003
  //   ,945,1855,166,8023,1646,1c05,ab,144,8003,155,1,444,166,7f,1646
  //   ,1c05,c0,17cc,1c04,e2,144,8,2344,144,20,2344,144,8,2344,19cc,1b00
  //   ,e2,166,c,1646,1c05,cd,1e00,5a,1e00,7a,1cc,0,1b00,e2,166,d,1646
  //   ,1c05,dc,2344,144,a,2344,1e00,7a,1cc,0,1b00,e2,166,8024,96c,364
  //   ,2344,18cc,166,8000,36c,166,8002,365,7c0,770,760,750,740,201,710
  //   ,1f00,6e,65,6f,66,65,74,63,68,0,1,0,1e00,5a,1e00,7a,2000,1e00
  //   ,8b,1b00,100
endmodule
