// Digital circuit CPUv4_copy.dig as structural Verilog
module CPUv4_copy (
  input  c,
  input  [15:0] bus_in,
  input  rd,
  input  irq,
  output [15:0] bus_out,
  output [15:0] addr_out,
  output [7:0] instr_out
);

  wire and_2_out, and_3_out, and_4_out, clock, d_ff_as_1_q, demultiplexer_1_out_0, demultiplexer_1_out_1,
       diodebackward_1_out, diodeforward_1_out, flag_en, flag_out, flag_str, hlt, i_o_in, i_o_out, instr_str,
       \int , int_en, jmp_en, mem_out, mem_str, multiplexer_5_out, nand_1_out, not_1_out, not_2_out,
       not_3_out, not_4_out, not_5_out, not_6_out, not_7_out, not_9_out, or_1_out, or_2_out, pc_en, pc_out,
       pc_str, reg_out, reg_str, sp_da, tx_da;
  wire [1:0] step_out;
  wire [3:0] alu_op, aluv4_1_v, jmp_ctrl, multiplexer_4_out, reg_des, reg_src;
  wire [7:4] instr_q;
  wire [14:0] multiplexer_11_out;
  wire [14:4] flag_q;
  wire [15:0] add_1_s, driver_6_out, multiplexer_1_out, multiplexer_2_out, multiplexer_3_out,
       multiplexer_7_out, multiplexer_8_out, multiplexer_9_out, multiplexer_10_out, pc_out_2,
       registerfile_1_da, registerfile_1_db;
  wire [15:15] int_q;

  assign bus_out = jmp_en ? multiplexer_1_out : 16'bz;  // Driver driver_1
  D_FF_AS d_ff_as_1 (.Set(rd), .D(rd), .C(and_3_out), .Clr(1'b0), .Q(d_ff_as_1_q));  // open: nQ
  and and_1 (clock, d_ff_as_1_q, c);
  and and_2 (and_2_out, irq, \int );
  and and_3 (and_3_out, ~jmp_en, instr_str);  // And
  Multiplexer #(.Bits(16)) multiplexer_1 (
    .sel(multiplexer_5_out), .in_0(16'h1d00), .in_1(16'h1b00), .out(multiplexer_1_out));
  Multiplexer #(.Bits(16)) multiplexer_2 (
    .sel(and_2_out), .in_0(multiplexer_3_out), .in_1(16'h2100), .out(multiplexer_2_out));
  Register #(.Bits(16)) instr (.D(multiplexer_2_out), .C(clock), .en(instr_str), .Q({instr_out, instr_q, reg_src}));
  Multiplexer #(.Bits(16)) multiplexer_3 (.sel(hlt), .in_0(bus_out), .in_1(16'h2500), .out(multiplexer_3_out));
  not not_1 (not_1_out, hlt);
  not not_2 (not_2_out, tx_da);
  Multiplexer #(.Bits(4)) multiplexer_4 (.sel(not_2_out), .in_0(4'b1111), .in_1(reg_des), .out(multiplexer_4_out));
  Multiplexer #(.Selector_Bits(3)) multiplexer_5 (
    .sel(reg_src[2:0]), .in_0(jmp_ctrl[0]), .in_1(not_6_out), .in_2(jmp_ctrl[1]), .in_3(not_5_out),
    .in_4(jmp_ctrl[2]), .in_5(not_4_out), .in_6(jmp_ctrl[3]), .in_7(not_3_out), .out(multiplexer_5_out));
  Counter #(.Bits(2)) step (.en(not_1_out), .C(clock), .clr(instr_str), .out(step_out));  // open: ovf
  or or_1 (or_1_out, i_o_in, mem_out);
  not not_3 (not_3_out, jmp_ctrl[3]);
  not not_4 (not_4_out, jmp_ctrl[2]);
  not not_5 (not_5_out, jmp_ctrl[1]);
  not not_6 (not_6_out, jmp_ctrl[0]);
  not not_7 (not_7_out, sp_da);
  Multiplexer #(.Bits(4)) multiplexer_6 (.sel(not_7_out), .in_0(4'b0000), .in_1(instr_q), .out(reg_des));
  Multiplexer #(.Bits(16)) multiplexer_7 (.sel(or_1_out), .in_0(addr_out), .in_1(bus_out), .out(multiplexer_7_out));
  RegisterFile #(.AddrBits(4), .Bits(16)) registerfile_1 (
    .Din(multiplexer_7_out), .we(reg_str), .Rw(multiplexer_4_out), .C(clock), .Ra(reg_des), .Rb(reg_src),
    .Da(registerfile_1_da), .Db(registerfile_1_db));
  ROM #(.AddrBits(10), .Bits(22)) rom_1 (
    .A({instr_out, step_out}), .sel(1'b1),
    .D({hlt, int_en, jmp_en, tx_da, sp_da, i_o_in, i_o_out, flag_out, flag_str, flag_en, alu_op, reg_str, reg_out, mem_str, mem_out, instr_str, pc_str, pc_out, pc_en}));
  assign bus_out = reg_out ? registerfile_1_db : 16'bz;  // Driver driver_2
  Multiplexer #(.Bits(16)) multiplexer_8 (
    .sel(reg_out), .in_0(registerfile_1_db), .in_1(registerfile_1_da), .out(multiplexer_8_out));
  ALUv4 aluv4_1 (
    .A(registerfile_1_da), .B(multiplexer_8_out), .C_in(jmp_ctrl[0]), .op(alu_op), .C_out(aluv4_1_v[0]),
    .Y(addr_out), .Z(aluv4_1_v[2]), .S(aluv4_1_v[1]), .V(aluv4_1_v[3]));
  Multiplexer #(.Bits(16)) multiplexer_9 (
    .sel(flag_str), .in_0({\int , {11{1'b0}}, aluv4_1_v}), .in_1(bus_out), .out(multiplexer_9_out));
  Multiplexer #(.Bits(16)) multiplexer_10 (.sel(int_en), .in_0(bus_out), .in_1(16'h10), .out(multiplexer_10_out));
  and and_4 (and_4_out, mem_out, ~pc_en);  // And
  not not_8 (\int , int_q[15]);
  Register u_int (.D(multiplexer_9_out[15]), .C(clock), .en(int_en), .Q(int_q[15]));
  not not_9 (not_9_out, addr_out[15]);
  Demultiplexer demultiplexer_1 (
    .sel(not_9_out), .in(and_4_out), .out_0(demultiplexer_1_out_0), .out_1(demultiplexer_1_out_1));
  CounterPreset #(.Bits(16), .isProgramCounter("true")) pc (
    .en(pc_en), .C(clock), .dir(1'b0), .in(multiplexer_10_out), .ld(pc_str), .clr(1'b0), .out(pc_out_2));  // open: ovf
  Register #(.Bits(15)) flag (.D(multiplexer_9_out[14:0]), .C(clock), .en(flag_en), .Q({flag_q, jmp_ctrl}));
  or or_2 (or_2_out, demultiplexer_1_out_1, pc_en);
  RAMSinglePort #(.AddrBits(15), .Bits(16)) ramsingleport_1 (
    .A(addr_out[14:0]), .str(mem_str), .C(clock), .ld(demultiplexer_1_out_0), .D(bus_out));
  Multiplexer #(.Bits(15)) multiplexer_11 (
    .sel(demultiplexer_1_out_1), .in_0(pc_out_2[14:0]), .in_1(addr_out[14:0]), .out(multiplexer_11_out));
  assign bus_out = flag_out ? {int_q[15], flag_q, jmp_ctrl} : 16'bz;  // Driver driver_3
  Add #(.Bits(16)) add_1 (.a(pc_out_2), .b({16{1'b0}}), .c_i(1'b1), .s(add_1_s));  // open: c_o
  ROM #(.AddrBits(15), .Bits(16)) rom_2 (.A(multiplexer_11_out), .sel(or_2_out), .D(bus_out));
  assign bus_out = pc_out ? add_1_s : 16'bz;  // Driver driver_4
  assign bus_out = i_o_in ? bus_in : 16'bz;  // Driver driver_5
  assign driver_6_out = i_o_out ? bus_out : 16'bz;  // Driver driver_6
  DiodeForward diodeforward_1 (.in(driver_6_out[8]), .out(diodeforward_1_out));
  PullDown pulldown_1 (.out(diodeforward_1_out));
  DiodeBackward diodebackward_1 (.in(driver_6_out[8]), .out(diodebackward_1_out));
  PullUp pullup_1 (.out(diodebackward_1_out));
  nand nand_1 (nand_1_out, diodebackward_1_out, ~diodeforward_1_out);  // NAnd
  Terminal terminal_1 (.D(driver_6_out[7:0]), .C(clock), .en(nand_1_out));

  // Other names for the same wires on the sheet: instr[7:0] = instr_out; addr[15:0] = addr_out; bus[15:0] = bus_out

  // Notes on the sheet:
  //   c: Hz: 2147483647
  //   rd: default 1
  //   contents of rom_1 (hex, n*v repeats v):
  //   9,0,0,0,91,9,0,0,89,0,0,0,60,9,0,0,90,9,0,0,20fe0,9,0,0,24fa0
  //   ,9,0,0,90,20e89,0,0,3010,20e89,0,0,1189,0,0,0,1289,0,0,0,1389
  //   ,0,0,0,1489,0,0,0,1589,0,0,0,1689,0,0,0,1789,0,0,0,41780,1689
  //   ,0,0,1889,0,0,0,1989,0,0,0,1a89,0,0,0,1c89,0,0,0,1d89,0,0,0,1309
  //   ,0,0,0,1009,0,0,0,1e89,0,0,0,1f89,0,0,0,1b89,0,0,0,5,9,0,0,80008
  //   ,0,0,0,1,9,0,0,20fa2,5,9,0,20014,20e89,0,0,100009,0,0,0,20fa2
  //   ,124fa4,9,0,123010,20e80,20014,20e89,8040,9,0,0,10080,9,0,0,200008
  //   contents of rom_2 (hex, n*v repeats v):
  //   2000,144,0,155,1,166,a,188,8000,298,1aa,30,274,1076,600,38f,1888
  //   ,800,1c05,d,1988,478,97a,2377,1698,1c05,14,177,a,2377,2b4,945
  //   ,25b,1c01,c,2500
endmodule
