// Digital circuit D_LATCH.dig as structural Verilog
module D_LATCH (
  input  [15:0] D,
  input  en,
  output [15:0] Q
);

  Multiplexer #(.Bits(16)) multiplexer_1 (.sel(en), .in_0(Q), .in_1(D), .out(Q));
endmodule
