// Digital circuit INT_HANDLER.dig as structural Verilog
module INT_HANDLER (
  input  INT_en,
  input  IRQ,
  input  C,
  output INT,
  output S
);

  wire and_1_out, d_ff_1_q, demultiplexer_1_out_0, demultiplexer_1_out_1, rs_ff_1_nq;

  D_FF d_ff_1 (.D(INT_en), .C(C), .Q(d_ff_1_q));  // open: nQ
  Demultiplexer demultiplexer_1 (
    .sel(d_ff_1_q), .in(INT_en), .out_0(demultiplexer_1_out_0), .out_1(demultiplexer_1_out_1));
  RS_FF rs_ff_1 (.S(demultiplexer_1_out_0), .C(C), .R(demultiplexer_1_out_1), .Q(S), .nQ(rs_ff_1_nq));
  and and_1 (and_1_out, rs_ff_1_nq, IRQ);
  RS_FF rs_ff_2 (.S(and_1_out), .C(C), .R(S), .Q(INT));  // open: nQ
endmodule
