// Digital circuit PULSE_EXTEND.dig as structural Verilog
module PULSE_EXTEND (
  input  C,
  input  in,
  output out
);

  wire d_ff_1_q, d_ff_2_q, or_1_out;

  D_FF d_ff_1 (.D(in), .C(C), .Q(d_ff_1_q));  // open: nQ
  or or_1 (or_1_out, in, d_ff_1_q);
  D_FF d_ff_2 (.D(or_1_out), .C(C), .Q(d_ff_2_q));  // open: nQ
  or or_2 (out, in, d_ff_2_q);
endmodule
