// Digital circuit SHIFT REG.dig as structural Verilog
module SHIFT_REG (
  input  [7:0] D,
  input  en,
  input  C,
  output [15:0] Q
);

  Register #(.Bits(8)) register_1 (.D(D), .C(C), .en(en), .Q(Q[7:0]));
  Register #(.Bits(8)) register_2 (.D(Q[7:0]), .C(C), .en(en), .Q(Q[15:8]));
endmodule
